# Fritzing sketch humidity-sensor-schematic (saved by Fritzing 0.9.3b)
breadboards: 1

parts:
  GC-58 = Humidity Sensor - HIH-4030 Breakout
  Part1 = Arduino Uno (Rev3) - ICSP
  HC-05 = Bluetooth Mate Silver

nets:
  GND: GC-58.GND, Part1.GND, HC-05.GND
  N1: GC-58.OUT, Part1.A0
  VCC: GC-58.VCC, Part1.5V, HC-05.VCC
  N2: Part1.D10_PWM/SS, HC-05.RX_5V
  N3: Part1.D11_PWM/MOSI, HC-05.TX_5V

// code stored in the sketch: humidity-sensor-breadboard.ino
#include <SoftwareSerial.h>

/*
	Connect BT module TX to D10
	Connect BT module RX to D11
	Connect BT Vcc to 5V, GND to GND
*/

SoftwareSerial BT(11, 10);
int sensor1;
String hash;
String sensorData;

void setup() {
   BT.begin(9600);
}

void loop() {
  sensor1 = analogRead(0);
  /*
	[
		{
			"name":"sensor_1",
			"data":"300"
		},
		{
			"name":"sensor_2",
			"data":"400"
		}
	]
	*/
  sensorData = String(sensor1);
  hash = "[{\"name\": \"sensor_1\", \"data\" :" + sensorData + " }]";

  BT.println(hash);
  /*
    TODO: Set this timer to get
    data each 15 minutes.

    The value above is for test only.
  */
  delay(1000);
}
