# Fritzing sketch watering-device (saved by Fritzing 0.9.3b)
breadboards: 1

parts:
  U1 = NodeMCU V1.0
  KY-1 = Keyes Relay [package=THT]
  VCC1 = Battery block 9V
  M1 = DC Motor

nets:
  N1: U1.3V3, KY-1.power
  N2: U1.GND, KY-1.ground
  N3: U1.D7, KY-1.signal
  N4: KY-1.NC, M1.pin_1
  N5: KY-1.C, VCC1.+

custom parts:
  NodeMCU V1.0: ESP8266 based NodeMCU
  Keyes Relay: The Keyes 5V relay module is suitable for SCM development, home appliance control. It uses a 5V~12V TIL control signal which can control DC / AC signal.
